// Logisim project CS1410_U201414830_方成_alu.circ as structural Verilog: 7 circuits, main circuit ALU
module ALU (
  input  [31:0] X,
  input  [31:0] Y,
  input  [3:0] AluOP,
  output Signed_Overflow,
  output UnSigned_Overflow,
  output Equal,
  output [31:0] Result,
  output [31:0] Result_2
);

  wire ADDOF_out, and_2_out, and_3_out, and_4_out, and_5_out, comparator_1_lt, comparator_2_lt,
       n32_bits_1_cout, n32_bits_2_cout, not_2_out, ns_f_2_out, ns_f_out, nx_f_out, ny_f_out, SUBOF_out;
  wire [31:0] and_1_out, bit_extender_1_out, bit_extender_2_out, divider_1_out, divider_1_rem,
       multiplier_1_cout, multiplier_1_out, n32_bits_1_s, n32_bits_2_s, nor_1_out, not_1_out, or_1_out,
       shifter_1_out, shifter_2_out, shifter_3_out, xor_1_out;

  // Probe on X
  // Probe on X
  not nx_f (nx_f_out, X[31]);
  // Probe on Y
  // Probe on Y
  not ny_f (ny_f_out, Y[31]);
  assign not_1_out = ~Y;  // NOT_Gate not_1, 32 bits wide
  Shifter #(.width(32)) shifter_1 (.in(X), .\dist (Y[4:0]), .out(shifter_1_out));
  Shifter #(.width(32), .shift("ar")) shifter_2 (.in(X), .\dist (Y[4:0]), .out(shifter_2_out));
  Shifter #(.width(32), .shift("lr")) shifter_3 (.in(X), .\dist (Y[4:0]), .out(shifter_3_out));
  Multiplier #(.width(32)) multiplier_1 (
    .a(X), .b(Y), .out(multiplier_1_out), .cin({32{1'b0}}), .cout(multiplier_1_cout));
  Divider #(.width(32)) divider_1 (.a(X), .b(Y), .out(divider_1_out), .upper({32{1'b0}}), .rem(divider_1_rem));
  _32_bits u_32_bits_1 (.X(X), .Y(Y), .Cout(n32_bits_1_cout), .S(n32_bits_1_s), .C0(1'b0));
  _32_bits u_32_bits_2 (.X(X), .Y(not_1_out), .Cout(n32_bits_2_cout), .S(n32_bits_2_s), .C0(1'b1));
  Comparator #(.width(32)) comparator_1 (.a(X), .b(Y), .eq(Equal), .lt(comparator_1_lt));  // open: gt
  Comparator #(.width(32), .mode("unsigned")) comparator_2 (.a(X), .b(Y), .lt(comparator_2_lt));  // open: gt, eq
  // Probe on AluOP
  not ns_f (ns_f_out, n32_bits_1_s[31]);
  assign and_1_out = X & Y;  // AND_Gate and_1, 32 bits wide
  assign or_1_out = X | Y;  // OR_Gate or_1, 32 bits wide
  not not_2 (not_2_out, n32_bits_2_cout);
  assign xor_1_out = X ^ Y;  // XOR_Gate xor_1, 32 bits wide
  assign nor_1_out = ~(X | Y);  // NOR_Gate nor_1, 32 bits wide
  assign bit_extender_1_out = {{31{1'b0}}, comparator_1_lt};  // Bit_Extender bit_extender_1
  assign bit_extender_2_out = {{31{1'b0}}, comparator_2_lt};  // Bit_Extender bit_extender_2
  // Probe on Result
  // Probe on Result
  and and_2 (and_2_out, X[31], Y[31], ns_f_out);
  and and_3 (and_3_out, nx_f_out, ny_f_out, n32_bits_1_s[31]);
  // Probe on Result_2
  or ADDOF (ADDOF_out, and_2_out, and_3_out);
  not ns_f_2 (ns_f_2_out, n32_bits_2_s[31]);
  and and_4 (and_4_out, X[31], ny_f_out, ns_f_2_out);
  and and_5 (and_5_out, nx_f_out, Y[31], n32_bits_2_s[31]);
  or SUBOF (SUBOF_out, and_4_out, and_5_out);
  Multiplexer #(.select(4), .width(32), .enable("false")) multiplexer_1 (
    .in0(shifter_1_out), .in1(shifter_2_out), .in2(shifter_3_out), .in3(multiplier_1_out),
    .in4(divider_1_out), .in5(n32_bits_1_s), .in6(n32_bits_2_s), .in7(and_1_out), .in8(or_1_out),
    .in9(xor_1_out), .in10(nor_1_out), .in11(bit_extender_1_out), .in12(bit_extender_2_out),
    .in13({32{1'b0}}), .in14({32{1'b0}}), .in15({32{1'b0}}), .out(Result), .sel(AluOP));
  Multiplexer #(.select(4), .width(32), .enable("false")) multiplexer_2 (
    .in0({32{1'b0}}), .in1({32{1'b0}}), .in2({32{1'b0}}), .in3(multiplier_1_cout), .in4(divider_1_rem),
    .in5({32{1'b0}}), .in6({32{1'b0}}), .in7({32{1'b0}}), .in8({32{1'b0}}), .in9({32{1'b0}}),
    .in10({32{1'b0}}), .in11({32{1'b0}}), .in12({32{1'b0}}), .in13({32{1'b0}}), .in14({32{1'b0}}),
    .in15({32{1'b0}}), .out(Result_2), .sel(AluOP));
  Multiplexer #(.select(4), .enable("false")) multiplexer_3 (
    .in0(1'b0), .in1(1'b0), .in2(1'b0), .in3(1'b0), .in4(1'b0), .in5(n32_bits_1_cout), .in6(not_2_out),
    .in7(1'b0), .in8(1'b0), .in9(1'b0), .in10(1'b0), .in11(1'b0), .in12(1'b0), .in13(1'b0), .in14(1'b0),
    .in15(1'b0), .out(UnSigned_Overflow), .sel(AluOP));
  Multiplexer #(.select(4), .enable("false")) multiplexer_4 (
    .in0(1'b0), .in1(1'b0), .in2(1'b0), .in3(1'b0), .in4(1'b0), .in5(ADDOF_out), .in6(SUBOF_out), .in7(1'b0),
    .in8(1'b0), .in9(1'b0), .in10(1'b0), .in11(1'b0), .in12(1'b0), .in13(1'b0), .in14(1'b0), .in15(1'b0),
    .out(Signed_Overflow), .sel(AluOP));

  // Other names for the same wires on the sheet: OF = Signed_Overflow; Result2[31:0] = Result_2; S[3:0] = AluOP;
  //   UOF = UnSigned_Overflow

  // Notes on the sheet:
  //   不要改变此引脚区域内容，也不要改变ALU封装形式
  //   输入引脚
  //   请在下方利用上方输入输出引脚的隧道信号构建ALU电路，ctrl+d复制选择部件
  //   华中科技大学计算机学院 计算机组成原理，鸣谢加州大学伯克利CS61C课程
  //   输出引脚
  //   探测区域
  //   ADD OF:(x_f&y_f&!s_f)|(!x_f&!y_f&s_f)
  //   SUB OF:(x_f&!y_f&!s_f)|(!x_f&y_f&s_f)
endmodule

module \演示电路  (
  input  [31:0] X,
  input  [31:0] Y,
  input  [3:0] ALUOP,
  output Signed_Overflow,
  output Unsigned_overflow,
  output [31:0] Result,
  output [31:0] Result_2,
  output Equal
);

  // Probe on X
  // Probe on X
  ALU alu_1 (
    .AluOP(ALUOP), .X(X), .Equal(Equal), .Result(Result), .Signed_Overflow(Signed_Overflow), .Y(Y),
    .Result_2(Result_2), .UnSigned_Overflow(Unsigned_overflow));
  // Probe on ALUOP
  // Probe on Y
  // Probe on Y
  // Probe on Result
  // Probe on Result
  // Probe on Result_2

  // Notes on the sheet:
  //   ALu电路无需调整位置即可连接在该电路中，并且不能出现蓝色线缆和三态输出
endmodule

module \等差数列  (
  input  [31:0] \数列初始值 ,
  input  [31:0] \等差值 ,
  input  \时钟 ,
  output [31:0] Result
);

  // Probe on \数列初始值 
  // Probe on \数列初始值 
  // Probe on \等差值 
  // Probe on \等差值 
  // Probe on Result
  // Probe on Result

  // Other names for the same wires on the sheet: 数列初值[31:0] = \数列初始值 ; 累加和[31:0] = Result

  // Notes on the sheet:
  //   不要改变此引脚区域内容，也不要改变ALU封装形式
  //   请在下方利用上方输入输出引脚的隧道信号构建等差数列求和电路，ctrl+d复制选择部件
  //   华中科技大学计算机学院 计算机组成原理，鸣谢加州大学伯克利CS61C课程
  //   输出引脚
  //   探测区域
endmodule

module _74182_carry (
  input  C0,
  input  [3:0] G,
  input  [3:0] P,
  output C1,
  output C2,
  output C3,
  output C4,
  output G4_star,
  output P4_star
);

  wire and_1_out, and_2_out, and_3_out, and_4_out, and_5_out, and_6_out, and_7_out, and_8_out, and_9_out,
       and_10_out, and_11_out, and_12_out, and_13_out;

  and and_1 (and_1_out, C0, P[0]);
  and and_2 (and_2_out, C0, P[0], P[1]);
  and and_3 (and_3_out, G[0], P[1]);
  and and_4 (and_4_out, C0, P[0], P[1], P[2]);
  and and_5 (and_5_out, G[0], P[1], P[2]);
  and and_6 (and_6_out, G[1], P[2]);
  and and_7 (and_7_out, C0, P[0], P[1], P[2], P[3]);
  and and_8 (and_8_out, G[0], P[2], P[1], P[3]);
  and and_9 (and_9_out, G[1], P[2], P[3]);
  and and_10 (and_10_out, G[2], P[3]);
  or u_C1 (C1, and_1_out, G[0]);
  or u_C2 (C2, and_2_out, G[1], and_3_out);
  or u_C3 (C3, G[2], and_4_out, and_5_out, and_6_out);
  or u_C4 (C4, G[3], and_7_out, and_8_out, and_9_out, and_10_out);
  and and_11 (and_11_out, P[3], G[2]);
  and and_12 (and_12_out, P[3], P[2], G[1]);
  and and_13 (and_13_out, P[3], P[2], P[1], G[0]);
  or C4_star (G4_star, G[3], and_11_out, and_12_out, and_13_out);
  and u_P4_star (P4_star, P[3], P[2], P[1], P[0]);
endmodule

module _4_bits (
  input  C0,
  input  [3:0] x,
  input  [3:0] y,
  output [3:0] S,
  output C4,
  output G4_star,
  output P4_star
);

  wire and_1_out, and_2_out, and_3_out, and_4_out, and_5_out, and_6_out, and_7_out, and_8_out, and_9_out,
       and_10_out, and_11_out, and_12_out, and_13_out, C1_out, C2_out, C3_out, G1_out, G2_out, G3_out,
       G4_out, P1_out, P2_out, P3_out, P4_out;

  and G1 (G1_out, x[0], y[0]);
  and G2 (G2_out, x[1], y[1]);
  and G3 (G3_out, x[2], y[2]);
  and G4 (G4_out, x[3], y[3]);
  xor P1 (P1_out, x[0], y[0]);
  xor P2 (P2_out, x[1], y[1]);
  xor P3 (P3_out, x[2], y[2]);
  xor P4 (P4_out, x[3], y[3]);
  and and_1 (and_1_out, C0, P1_out);
  and and_2 (and_2_out, C0, P1_out, P2_out);
  and and_3 (and_3_out, G1_out, P2_out);
  and and_4 (and_4_out, C0, P1_out, P2_out, P3_out);
  and and_5 (and_5_out, G1_out, P2_out, P3_out);
  and and_6 (and_6_out, G2_out, P3_out);
  and and_7 (and_7_out, C0, P1_out, P2_out, P3_out, P4_out);
  and and_8 (and_8_out, G1_out, P3_out, P2_out, P4_out);
  and and_9 (and_9_out, G2_out, P3_out, P4_out);
  and and_10 (and_10_out, G3_out, P4_out);
  or C1 (C1_out, and_1_out, G1_out);
  or C2 (C2_out, and_2_out, G2_out, and_3_out);
  or C3 (C3_out, G3_out, and_4_out, and_5_out, and_6_out);
  or u_C4 (C4, G4_out, and_7_out, and_8_out, and_9_out, and_10_out);
  xor S1 (S[0], C0, P1_out);
  xor S2 (S[1], P2_out, C1_out);
  xor S3 (S[2], P3_out, C2_out);
  xor S4 (S[3], P4_out, C3_out);
  and and_11 (and_11_out, P4_out, G3_out);
  and and_12 (and_12_out, P4_out, P3_out, G2_out);
  and and_13 (and_13_out, P4_out, P3_out, P2_out, G1_out);
  or u_G4_star (G4_star, G4_out, and_11_out, and_12_out, and_13_out);
  and u_P4_star (P4_star, P4_out, P3_out, P2_out, P1_out);
endmodule

module _16_bits (
  input  [15:0] X,
  input  [15:0] Y,
  input  C0,
  output [15:0] S,
  output Cout,
  output GS,
  output PS
);

  wire n74182_carry_1_c1, n74182_carry_1_c2, n74182_carry_1_c3;
  wire [3:0] n4_bits_4_g4_star, n4_bits_4_p4_star;

  _4_bits u_4_bits_1 (
    .x(X[15:12]), .y(Y[15:12]), .C0(n74182_carry_1_c3), .S(S[15:12]), .P4_star(n4_bits_4_p4_star[3]),
    .G4_star(n4_bits_4_g4_star[3]));  // open: C4
  _4_bits u_4_bits_2 (
    .x(X[11:8]), .y(Y[11:8]), .C0(n74182_carry_1_c2), .S(S[11:8]), .P4_star(n4_bits_4_p4_star[2]),
    .G4_star(n4_bits_4_g4_star[2]));  // open: C4
  _4_bits u_4_bits_3 (
    .x(X[7:4]), .y(Y[7:4]), .C0(n74182_carry_1_c1), .S(S[7:4]), .P4_star(n4_bits_4_p4_star[1]),
    .G4_star(n4_bits_4_g4_star[1]));  // open: C4
  _4_bits u_4_bits_4 (
    .x(X[3:0]), .y(Y[3:0]), .C0(C0), .S(S[3:0]), .P4_star(n4_bits_4_p4_star[0]),
    .G4_star(n4_bits_4_g4_star[0]));  // open: C4
  _74182_carry u_74182_carry_1 (
    .C0(C0), .C1(n74182_carry_1_c1), .C2(n74182_carry_1_c2), .C3(n74182_carry_1_c3), .C4(Cout), .G4_star(GS),
    .P4_star(PS), .G(n4_bits_4_g4_star), .P(n4_bits_4_p4_star));
endmodule

// +
module _32_bits (
  input  [31:0] X,
  input  [31:0] Y,
  input  C0,
  output Cout,
  output [31:0] S
);

  wire n74182_carry_1_c1, n74182_carry_1_c3;
  wire [3:0] n16_bits_4_gs, n16_bits_4_ps;

  _16_bits u_16_bits_1 (
    .X({16{1'b0}}), .Y({16{1'b0}}), .C0(n74182_carry_1_c3), .GS(n16_bits_4_gs[3]), .PS(n16_bits_4_ps[3]));  // open: S, Cout
  _16_bits u_16_bits_2 (
    .X({16{1'b0}}), .Y({16{1'b0}}), .C0(Cout), .GS(n16_bits_4_gs[2]), .PS(n16_bits_4_ps[2]));  // open: S, Cout
  _16_bits u_16_bits_3 (
    .X(X[31:16]), .Y(Y[31:16]), .S(S[31:16]), .C0(n74182_carry_1_c1), .GS(n16_bits_4_gs[1]),
    .PS(n16_bits_4_ps[1]));  // open: Cout
  _16_bits u_16_bits_4 (
    .X(X[15:0]), .Y(Y[15:0]), .S(S[15:0]), .C0(C0), .GS(n16_bits_4_gs[0]), .PS(n16_bits_4_ps[0]));  // open: Cout
  _74182_carry u_74182_carry_1 (
    .C0(C0), .C1(n74182_carry_1_c1), .C2(Cout), .C3(n74182_carry_1_c3), .G(n16_bits_4_gs), .P(n16_bits_4_ps));  // open: C4, G4_star, P4_star
endmodule
