// Logisim project CS1410_U201414830_方成_cpu.circ as structural Verilog: 10 circuits, main circuit main
module main (
  output [9:0] R_type,
  output [9:0] I_type,
  output [5:0] J_type
);

  wire alu_1_equal, ALUsrc, and_1_out, and_2_out, and_3_out, and_4_out, and_5_out, beq, BLEZ, bne, Branch,
       clk, clock_1_out, ExpBlock, ExpSrc0, ExpSrc1, ExpSrc2, ExRegWrite, HasExp, IsEret, IsException, Jal,
       jr, Jump, LH, LUI, MemRead, MemtoReg, MemWrite, multiplexer_3_out, multiplexer_19_out, not_1_out,
       not_2_out, not_3_out, not_4_out, or_1_out, or_2_out, or_3_out, RegDst, RegWrite, shfit, syscall,
       Zero_Extend;
  wire [3:0] OP_ALU;
  wire [4:0] multiplexer_5_out, multiplexer_6_out, multiplexer_7_out, multiplexer_8_out, multiplexer_9_out;
  wire [8:0] demultiplexer_1_out0, demultiplexer_1_out1;
  wire [11:0] counter_1_q;
  wire [27:0] adder_1_out;
  wire [31:0] a0, adder_2_out, alu_1_result, bit_extender_1_out, bit_extender_2_out, bit_extender_3_out,
       bit_extender_4_out, CodeIn, DIn, DOut, main_1_reg1, main_1_s1_value, multiplexer_1_out,
       multiplexer_2_out, multiplexer_10_out, multiplexer_11_out, multiplexer_12_out, multiplexer_13_out,
       multiplexer_14_out, multiplexer_15_out, multiplexer_16_out, multiplexer_17_out, multiplexer_18_out,
       multiplexer_20_out, multiplexer_21_out, multiplexer_22_out, multiplexer_23_out, PC_q, PcIn, PcOut,
       ram_1_data, rom_1_data, rom_2_data, shifter_1_out, shifter_2_out, shifter_3_out;

  Multiplexer #(.width(32), .enable("false")) multiplexer_1 (
    .in0(multiplexer_22_out), .in1(PcOut), .out(multiplexer_1_out), .sel(IsEret));
  Multiplexer #(.width(32), .enable("false")) multiplexer_2 (
    .in0(32'h800), .in1(multiplexer_1_out), .out(multiplexer_2_out), .sel(not_1_out));
  not not_1 (not_1_out, HasExp);
  or or_1 (or_1_out, HasExp, IsEret);
  Button button_1 (.out(ExpSrc0));
  Multiplexer #(.enable("false")) multiplexer_3 (.in0(clk), .in1(not_2_out), .out(multiplexer_3_out), .sel(or_1_out));
  not not_2 (not_2_out, clk);
  Button button_2 (.out(ExpSrc1));
  Register #(.width(32)) PC (.D(multiplexer_2_out), .Q(PC_q), .clk(multiplexer_3_out));  // open: en, clr
  Demultiplexer #(.width(9), .enable("false")) demultiplexer_1 (
    .out0(demultiplexer_1_out0), .out1(demultiplexer_1_out1), .in(PC_q[10:2]), .sel(PC_q[11]));
  Button button_3 (.out(ExpSrc2));
  Register #(.width(32)) PC_Buffer (.D(PC_q), .Q(PcIn), .clk(HasExp));  // open: en, clr
  Hex_Digit_Display hex_digit_display_1 (.value(a0[31:28]));  // open: dp
  Adder #(.width(32)) adder_1 (.a(32'h4), .b(PC_q), .out({shifter_1_out[31:28], adder_1_out}));  // open: cin, cout
  Hex_Digit_Display hex_digit_display_2 (.value(a0[23:20]));  // open: dp
  Hex_Digit_Display hex_digit_display_3 (.value(a0[27:24]));  // open: dp
  ROM #(.addrWidth(9), .dataWidth(32)) rom_1 (.addr(demultiplexer_1_out0), .data(rom_1_data));  // open: sel
  Multiplexer #(.width(32), .enable("false")) multiplexer_4 (
    .in0(rom_1_data), .in1(rom_2_data), .out(CodeIn), .sel(PC_q[11]));
  ROM #(.addrWidth(9), .dataWidth(32)) rom_2 (.addr(demultiplexer_1_out1), .data(rom_2_data));  // open: sel
  Hex_Digit_Display hex_digit_display_4 (.value(a0[19:16]));  // open: dp
  CP0 cp0_1 (
    .ExpSrc0(ExpSrc0), .clk(clk), .ExpSrc1(ExpSrc1), .enable(IsException), .ExpSrc2(ExpSrc2), .Inst(CodeIn),
    .PCin(PcIn), .Din(DIn), .ExRegWrite(ExRegWrite), .IsEret(IsEret), .ExpBlock(ExpBlock), .HasExp(HasExp),
    .PCout(PcOut), .Dout(DOut));
  Shifter #(.width(28)) shifter_1 (.in(CodeIn[27:0]), .\dist (5'b00010), .out(shifter_1_out[27:0]));
  Hex_Digit_Display hex_digit_display_5 (.value(a0[11:8]));  // open: dp
  Hex_Digit_Display hex_digit_display_6 (.value(a0[15:12]));  // open: dp
  Multiplexer #(.width(5), .enable("false")) multiplexer_5 (
    .in0(CodeIn[25:21]), .in1(CodeIn[20:16]), .out(multiplexer_5_out), .sel(shfit));
  Multiplexer #(.width(5), .enable("false")) multiplexer_6 (
    .in0(CodeIn[20:16]), .in1(CodeIn[15:11]), .out(multiplexer_6_out), .sel(RegDst));
  Hex_Digit_Display hex_digit_display_7 (.value(a0[7:4]));  // open: dp
  Hex_Digit_Display hex_digit_display_8 (.value(a0[3:0]));  // open: dp
  Multiplexer #(.width(5), .enable("false")) multiplexer_7 (
    .in0(multiplexer_5_out), .in1({5{1'b1}}), .out(multiplexer_7_out), .sel(jr));
  Multiplexer #(.width(5), .enable("false")) multiplexer_8 (
    .in0(multiplexer_7_out), .in1(5'b00010), .out(multiplexer_8_out), .sel(syscall));
  Multiplexer #(.width(5), .enable("false")) multiplexer_9 (
    .in0(multiplexer_6_out), .in1({5{1'b1}}), .out(multiplexer_9_out), .sel(Jal));
  assign bit_extender_1_out = {{16{CodeIn[15]}}, CodeIn[15:0]};  // Bit_Extender bit_extender_1
  assign bit_extender_2_out = {{16{1'b0}}, CodeIn[15:0]};  // Bit_Extender bit_extender_2
  Multiplexer #(.width(32), .enable("false")) multiplexer_10 (
    .in0(multiplexer_12_out), .in1(multiplexer_13_out), .out(multiplexer_10_out), .sel(LUI));
  Multiplexer #(.width(32), .enable("false")) multiplexer_11 (
    .in0(bit_extender_1_out), .in1(bit_extender_2_out), .out(multiplexer_11_out), .sel(Zero_Extend));
  Multiplexer #(.width(32), .enable("false")) multiplexer_12 (
    .in0(multiplexer_21_out), .in1({shifter_1_out[31:28], adder_1_out}), .out(multiplexer_12_out), .sel(Jal));
  // Probe on main_1_s1_value
  \CS1410_U201414830_方成_regfile_main  main_1 (
    .Reg1_num(multiplexer_8_out), .Reg2(CodeIn[20:16]), .Write_Reg_num(multiplexer_9_out),
    .Din(multiplexer_10_out), .Write_Enable(RegWrite), .Clock(clk), .Reg1(main_1_reg1), .Reg2_2(DIn),
    .s0_Value(a0), .s1_Value(main_1_s1_value));  // open: s2_Value, ra_Value, ra_Value_2
  Multiplexer #(.width(32), .enable("false")) multiplexer_13 (
    .in0(multiplexer_11_out), .in1(shifter_2_out), .out(multiplexer_13_out), .sel(LUI));
  Shifter #(.width(32)) shifter_2 (.in(multiplexer_11_out), .\dist (5'b10000), .out(shifter_2_out));
  // Probe on CodeIn[31:26]
  // Probe on CodeIn[5:0]
  Multiplexer #(.width(32), .enable("false")) multiplexer_14 (
    .in0(DIn), .in1(multiplexer_13_out), .out(multiplexer_14_out), .sel(ALUsrc));
  assign bit_extender_3_out = {{27{1'b0}}, CodeIn[10:6]};  // Bit_Extender bit_extender_3
  Shifter #(.width(32)) shifter_3 (.in(multiplexer_13_out), .\dist (5'b00010), .out(shifter_3_out));
  and and_1 (and_1_out, Branch, or_2_out);
  or or_2 (or_2_out, and_2_out, and_3_out);
  and and_2 (and_2_out, bne, not_3_out);
  not not_3 (not_3_out, alu_1_equal);
  Multiplexer #(.width(32), .enable("false")) multiplexer_15 (
    .in0(multiplexer_14_out), .in1(bit_extender_3_out), .out(multiplexer_15_out), .sel(shfit));
  Control_Unit Control_Unit (
    .OP(CodeIn[31:26]), .funct(CodeIn[5:0]), .out_3(RegWrite), .out_4(ALUsrc), .out_5(MemWrite),
    .out_6(Branch), .out_7(MemtoReg), .out_8(Jal), .out_9(Zero_Extend), .out_10(MemRead), .out_11(bne),
    .out_12(Jump), .out_13(beq), .out_14(RegDst), .out_15(shfit), .out_16(jr), .out_17(syscall),
    .out_18(OP_ALU), .out_19(LUI), .out_20(BLEZ), .out_21(LH), .out_22(IsException));
  Adder #(.width(32)) adder_2 (
    .a({shifter_1_out[31:28], adder_1_out}), .b(shifter_3_out), .out(adder_2_out));  // open: cin, cout
  and and_3 (and_3_out, alu_1_equal, beq);
  Multiplexer #(.width(32), .enable("false")) multiplexer_16 (
    .in0(multiplexer_15_out), .in1(32'ha), .out(multiplexer_16_out), .sel(syscall));
  Multiplexer #(.width(32), .enable("false")) multiplexer_17 (
    .in0(multiplexer_16_out), .in1({32{1'b0}}), .out(multiplexer_17_out), .sel(BLEZ));
  Multiplexer #(.width(32), .enable("false")) multiplexer_18 (
    .in0({shifter_1_out[31:28], adder_1_out}), .in1(adder_2_out), .out(multiplexer_18_out),
    .sel(multiplexer_19_out));
  Multiplexer #(.enable("false")) multiplexer_19 (
    .in0(and_1_out), .in1(and_4_out), .out(multiplexer_19_out), .sel(BLEZ));
  and and_4 (and_4_out, BLEZ, or_3_out);
  or or_3 (or_3_out, alu_1_equal, alu_1_result[0]);
  ALU alu_1 (
    .AluOP(OP_ALU), .X(main_1_reg1), .Equal(alu_1_equal), .Result(alu_1_result), .Y(multiplexer_17_out));  // open: Signed_Overflow, Result_2, UnSigned_Overflow
  // Probe on OP_ALU
  Clock clock_1 (.out(clock_1_out));
  and and_5 (and_5_out, syscall, alu_1_equal);
  Multiplexer #(.width(32), .enable("false")) multiplexer_20 (
    .in0(multiplexer_18_out), .in1(shifter_1_out), .out(multiplexer_20_out), .sel(Jump));
  and and_6 (clk, clock_1_out, not_4_out);
  not not_4 (not_4_out, and_5_out);
  Multiplexer #(.width(32), .enable("false")) multiplexer_21 (
    .in0(multiplexer_23_out), .in1(bit_extender_4_out), .out(multiplexer_21_out), .sel(LH));
  Multiplexer #(.width(32), .enable("false")) multiplexer_22 (
    .in0(multiplexer_20_out), .in1(main_1_reg1), .out(multiplexer_22_out), .sel(jr));
  // Probe on counter_1_q
  Counter #(.width(12), .max('hfff)) counter_1 (.Q(counter_1_q), .clk(clk));  // open: load, D, count, carry, clr
  RAM #(.addrWidth(24), .dataWidth(32), .bus("separate")) ram_1 (
    .addr(alu_1_result[25:2]), .din(DIn), .data(ram_1_data), .str(MemWrite), .clk(clk), .ld(MemRead));  // open: sel, clr
  // Probe on R_type
  // Probe on I_type
  Instructtion_type instructtion_type_1 (
    .OP(CodeIn[31:26]), .clk(clk), .out_3(R_type), .out_4(I_type), .J_type(J_type));
  // Probe on J_type
  Multiplexer #(.width(32), .enable("false")) multiplexer_23 (
    .in0(alu_1_result), .in1(ram_1_data), .out(multiplexer_23_out), .sel(MemtoReg));
  assign bit_extender_4_out = {{16{multiplexer_23_out[15]}}, multiplexer_23_out[15:0]};  // Bit_Extender bit_extender_4

  // Other names for the same wires on the sheet: funct[5:0] = CodeIn[5:0]; OP[5:0] = CodeIn[31:26]

  // Notes on the sheet:
  //   contents of rom_1 (hex, n*v repeats v):
  //   20110001 8100005 20110001 20120002 20130003 8100009 20110001 20120002 20130003 810000d 20110001
  //   20120002 20130003 8100011 20110001 20120002 20130003 c1000b8 20100001 20110001 118fc0 112020
  //   20020022 c 118882 12200001 8100015 112020 20020022 c 20110001 118880 112020 20020022 c 12200001
  //   810001f 20110001 118fc0 112020 20020022 c 1188c3 112020 20020022 c 118903 112020 20020022 c 118903
  //   112020 20020022 c 118903 112020 20020022 c 118903 112020 20020022 c 118903 112020 20020022 c 118903
  //   112020 20020022 c 118903 112020 20020022 c 20100001 109fc0 139fc3 8021 2012000c 24160003 26100001
  //   3210000f 20080008 20090001 139900 2709825 132020 20020022 c 1094022 1500fff9 22100001 2018000f
  //   2188024 108700 20080008 20090001 139902 2709825 132021 20020022 c 1094022 1500fff9 108702 2c9b022
  //   12c00001 8100050 4020 1084027 84400 3508ffff 82021 20020022 c 2010ffff 20110000 ae300000 22100001
  //   22310004 ae300000 22100001 22310004 ae300000 22100001 22310004 ae300000 22100001 22310004 ae300000
  //   22100001 22310004 ae300000 22100001 22310004 ae300000 22100001 22310004 ae300000 22100001 22310004
  //   ae300000 22100001 22310004 ae300000 22100001 22310004 ae300000 22100001 22310004 ae300000 22100001
  //   22310004 ae300000 22100001 22310004 ae300000 22100001 22310004 ae300000 22100001 22310004 ae300000
  //   22100001 22310004 22100001 8020 2011003c 8e130000 8e340000 274402a 11000002 ae330000 ae140000
  //   2231fffc 1611fff8 102020 20020022 c 22100004 2011003c 1611fff2 2002000a c 20100000 22100001 102020
  //   20020022 c 22100002 102020 20020022 c 22100003 102020 20020022 c 22100004 102020 20020022 c 22100005
  //   102020 20020022 c 22100006 102020 20020022 c 22100007 102020 20020022 c 22100008 102020 20020022
  //   20020022 c 3e00008
  //   contents of rom_2 (hex, n*v repeats v):
  //   201a0001 409a0800 201c0040 39df020 401a0000 afda0000 23de0004 23bd0004 afd00000 23bd0004 23de0004
  //   afd40000 23bd0004 23de0004 afd50000 23bd0004 23de0004 afd60000 23bd0004 23de0004 afc40000 23bd0004
  //   23de0004 afc20000 23bd0004 23de0004 40161000 22d60001 201a0000 409a0800 20140005 20150001 168020
  //   102020 20020022 c 108100 1600fffb 295a022 1680fff8 201a0001 409a0800 23defffc 23bdfffc 8fc20000
  //   23defffc 23bdfffc 8fc40000 23defffc 23bdfffc 8fd60000 23defffc 23bdfffc 8fd50000 23defffc 23bdfffc
  //   8fd40000 23defffc 23bdfffc 8fd00000 23defffc 23bdfffc 8fda0000 409a0000 201a0000 409a0800 42000018
  //   rs
  //   rt
  //   rd
  //   shamt
  //   条件调转
  //   无条件调转
  //   jr
endmodule

module Control_Unit (
  input  [5:0] OP,
  input  [5:0] funct,
  output out_3,
  output out_4,
  output out_5,
  output out_6,
  output out_7,
  output out_8,
  output out_9,
  output out_10,
  output out_11,
  output out_12,
  output out_13,
  output out_14,
  output out_15,
  output out_16,
  output out_17,
  output [3:0] out_18,
  output out_19,
  output out_20,
  output out_21,
  output out_22
);

  wire Add, AddI, AddIU, AddU, AND, AndI, ARL, is_R, J, JR, Lw, multiplexer_1_out, Nor, nor_2_out, not_1_out,
       not_3_out, not_4_out, not_5_out, Or, or_8_out, OrI, Sll, Slt, SltI, SltU, SRA, Sub, XOR;
  wire [3:0] ALU_OP, multiplexer_3_out, multiplexer_4_out, multiplexer_5_out;

  R_Control r_control_1 (
    .funct5(funct[5]), .funct4(funct[4]), .funct3(funct[3]), .funct2(funct[2]), .funct1(funct[1]),
    .funct0(funct[0]), .Add(Add), .AddU(AddU), .AND(AND), .Sll(Sll), .SRA(SRA), .SRL(ARL), .Sub(Sub),
    .Or(Or), .Nor(Nor), .Slt(Slt), .SltU(SltU), .JR(JR), .XOR(XOR));
  I_Control i_control_1 (
    .OP5(OP[5]), .OP4(OP[4]), .OP3(OP[3]), .OP2(OP[2]), .OP1(OP[1]), .OP0(OP[0]), .AddI(AddI), .AddIU(AddIU),
    .AndI(AndI), .OrI(OrI), .Lw(Lw), .Sw(out_5), .Beq(out_13), .Bne(out_11), .SltI(SltI), .J(J), .JAL(out_8),
    .LUI(out_19), .BLEZ(out_20), .LH(out_21));
  or or_1 (out_4, AddI, AddIU, AndI, OrI, Lw, out_5, SltI, out_21);
  or or_2 (out_12, J, out_8);
  or or_3 (out_6, out_13, out_20, out_11);
  not not_1 (not_1_out, funct[5]);
  and and_1 (out_15, is_R, not_1_out, multiplexer_1_out);
  nor nor_1 (out_14, OP[5], OP[4], OP[3], OP[2], OP[1], OP[0]);
  or or_4 (out_7, Lw, out_21);
  Multiplexer #(.select(2), .enable("false")) multiplexer_1 (
    .in0(1'b1), .in2(1'b1), .in3(1'b1), .out(multiplexer_1_out), .sel(funct[1:0]));  // open: in1
  and and_2 (out_22, ~OP[5], OP[4], ~OP[3], ~OP[2], ~OP[1], ~OP[0]);  // AND_Gate
  or or_5 (out_9, AndI, AddIU, OrI);
  Multiplexer #(.select(4), .width(4), .enable("false")) multiplexer_2 (
    .in0(4'b0000), .in1(4'b0101), .in2(4'b1111), .in3(4'b0101), .in4(4'b0101), .in5(4'b0101), .in6(4'b1011),
    .in7(4'b1111), .in8(4'b0101), .in9(4'b0101), .in10(4'b1011), .in11(4'b0101), .in12(4'b0111),
    .in13(4'b1000), .in14(4'b1111), .in15(4'b1111), .out(ALU_OP), .sel(OP[3:0]));
  Multiplexer #(.select(2), .width(4), .enable("false")) multiplexer_3 (
    .in0(4'b0000), .in2(4'b0010), .in3(4'b0001), .out(multiplexer_3_out), .sel(funct[1:0]));  // open: in1
  Multiplexer #(.select(4), .width(4), .enable("false")) multiplexer_4 (
    .in0(4'b0101), .in1(4'b0101), .in2(4'b0110), .in3(4'b1111), .in4(4'b0111), .in5(4'b1000), .in6(4'b1001),
    .in7(4'b1010), .in8(4'b1111), .in9(4'b1111), .in10(4'b1011), .in11(4'b1100), .in12(4'b1111),
    .in13(4'b1111), .in14(4'b1111), .in15(4'b1111), .out(multiplexer_4_out), .sel(funct[3:0]));
  or or_6 (out_10, Lw, out_21);
  // Probe on ALU_OP
  Multiplexer #(.width(4), .enable("false")) multiplexer_5 (
    .in0(multiplexer_3_out), .in1(multiplexer_4_out), .out(multiplexer_5_out), .sel(funct[5]));
  or or_7 (out_3, out_14, AddI, AddIU, AndI, out_8, SltI, Lw, OrI, out_19, out_21);
  or or_8 (or_8_out, ALU_OP[3], ALU_OP[2], ALU_OP[1], ALU_OP[0]);
  not not_2 (is_R, or_8_out);
  // Probe on out_18
  Multiplexer #(.width(4), .enable("false")) multiplexer_6 (
    .in0(multiplexer_5_out), .in1(ALU_OP), .out(out_18), .sel(not_3_out));
  not not_3 (not_3_out, is_R);
  and and_3 (out_16, is_R, JR);
  and and_4 (out_17, is_R, nor_2_out);
  not not_4 (not_4_out, funct[2]);
  not not_5 (not_5_out, funct[3]);
  nor nor_2 (nor_2_out, funct[5], funct[4], not_5_out, not_4_out, funct[1], funct[0]);

  // Other names for the same wires on the sheet: ALUsrc = out_4; Beq = out_13; BLEZ = out_20; Bne = out_11;
  //   Branch = out_6; f2_f1[1:0] = funct[1:0]; f4_f1[3:0] = funct[3:0]; f6 = funct[5]; IsException = out_22;
  //   JAL = out_8; jr_t = out_16; Jump = out_12; LH = out_21; LUI = out_19; MemRead = out_10; MemtoReg = out_7;
  //   op_t[3:0] = OP[3:0]; OP_ALU[3:0] = out_18; R_type = out_14; RegDst = out_14; RegWrite = out_3; shfit = out_15;
  //   MemWrite = out_5; Sw = out_5; syscall = out_17; Zero_Extend = out_9

  // Notes on the sheet:
  //   shift
endmodule

module R_Control (
  input  funct5,
  input  funct4,
  input  funct3,
  input  funct2,
  input  funct1,
  input  funct0,
  output Add,
  output AddU,
  output AND,
  output Sll,
  output SRA,
  output SRL,
  output Sub,
  output Or,
  output Nor,
  output Slt,
  output SltU,
  output JR,
  output XOR
);

  wire not_1_out, not_2_out, not_3_out, not_4_out, not_5_out, not_6_out, not_7_out, not_8_out, not_9_out,
       not_10_out, not_11_out, not_12_out, not_13_out, not_14_out, not_15_out, not_16_out, not_17_out,
       not_18_out, not_19_out, not_20_out, not_21_out, not_22_out, not_23_out, not_24_out, not_25_out,
       not_26_out, not_27_out, not_28_out, not_29_out, not_30_out, not_31_out, not_32_out, not_33_out,
       not_34_out, not_35_out, not_36_out, not_37_out, not_38_out, not_39_out, not_40_out, not_41_out,
       not_42_out, not_43_out, not_44_out, not_45_out, not_46_out, not_47_out, not_48_out, not_49_out,
       not_50_out;

  not not_1 (not_1_out, funct4);
  not not_2 (not_2_out, funct3);
  not not_3 (not_3_out, funct2);
  not not_4 (not_4_out, funct1);
  not not_5 (not_5_out, funct0);
  not not_6 (not_6_out, funct4);
  not not_7 (not_7_out, funct3);
  not not_8 (not_8_out, funct2);
  not not_9 (not_9_out, funct1);
  not not_10 (not_10_out, funct4);
  not not_11 (not_11_out, funct3);
  not not_12 (not_12_out, funct1);
  not not_13 (not_13_out, funct0);
  not not_14 (not_14_out, funct5);
  not not_15 (not_15_out, funct4);
  not not_16 (not_16_out, funct3);
  not not_17 (not_17_out, funct2);
  not not_18 (not_18_out, funct1);
  not not_19 (not_19_out, funct0);
  not not_20 (not_20_out, funct5);
  not not_21 (not_21_out, funct4);
  not not_22 (not_22_out, funct3);
  not not_23 (not_23_out, funct2);
  not not_24 (not_24_out, funct5);
  not not_25 (not_25_out, funct4);
  not not_26 (not_26_out, funct3);
  not not_27 (not_27_out, funct2);
  not not_28 (not_28_out, funct0);
  not not_29 (not_29_out, funct4);
  not not_30 (not_30_out, funct3);
  not not_31 (not_31_out, funct2);
  not not_32 (not_32_out, funct0);
  not not_33 (not_33_out, funct4);
  not not_34 (not_34_out, funct3);
  not not_35 (not_35_out, funct1);
  not not_36 (not_36_out, funct4);
  not not_37 (not_37_out, funct3);
  not not_38 (not_38_out, funct4);
  not not_39 (not_39_out, funct2);
  not not_40 (not_40_out, funct0);
  not not_41 (not_41_out, funct4);
  not not_42 (not_42_out, funct2);
  not not_43 (not_43_out, funct5);
  not not_44 (not_44_out, funct4);
  not not_45 (not_45_out, funct2);
  not not_46 (not_46_out, funct1);
  not not_47 (not_47_out, funct0);
  not not_48 (not_48_out, funct4);
  not not_49 (not_49_out, funct3);
  not not_50 (not_50_out, funct0);
  and and_1 (Add, funct5, not_1_out, not_2_out, not_3_out, not_4_out, not_5_out);
  and and_2 (AddU, funct5, not_6_out, not_7_out, not_8_out, not_9_out, funct0);
  and and_3 (AND, funct5, not_10_out, not_11_out, funct2, not_12_out, not_13_out);
  and and_4 (Sll, not_14_out, not_15_out, not_16_out, not_17_out, not_18_out, not_19_out);
  and and_5 (SRA, not_20_out, not_21_out, not_22_out, not_23_out, funct1, funct0);
  and and_6 (SRL, not_24_out, not_25_out, not_26_out, not_27_out, funct1, not_28_out);
  and and_7 (Sub, funct5, not_29_out, not_30_out, not_31_out, funct1, not_32_out);
  and and_8 (Or, funct5, not_33_out, not_34_out, funct2, not_35_out, funct0);
  and and_9 (Nor, funct5, not_36_out, not_37_out, funct2, funct1, funct0);
  and and_10 (Slt, funct5, not_38_out, funct3, not_39_out, funct1, not_40_out);
  and and_11 (SltU, funct5, not_41_out, funct3, not_42_out, funct1, funct0);
  and and_12 (JR, not_43_out, not_44_out, funct3, not_45_out, not_46_out, not_47_out);
  and and_13 (XOR, funct5, not_48_out, not_49_out, funct2, funct1, not_50_out);
endmodule

module I_Control (
  input  OP5,
  input  OP4,
  input  OP3,
  input  OP2,
  input  OP1,
  input  OP0,
  output AddI,
  output AddIU,
  output AndI,
  output OrI,
  output Lw,
  output Sw,
  output Beq,
  output Bne,
  output SltI,
  output J,
  output JAL,
  output LUI,
  output BLEZ,
  output LH
);

  wire not_1_out, not_2_out, not_3_out, not_4_out, not_5_out, not_6_out, not_7_out, not_8_out, not_9_out,
       not_10_out, not_11_out, not_12_out, not_13_out, not_14_out, not_15_out, not_16_out, not_17_out,
       not_18_out, not_19_out, not_20_out, not_21_out, not_22_out, not_23_out, not_24_out, not_25_out,
       not_26_out, not_27_out, not_28_out, not_29_out, not_30_out, not_31_out, not_32_out, not_33_out,
       not_34_out, not_35_out, not_36_out, not_37_out, not_38_out, not_39_out, not_40_out, not_41_out,
       not_42_out, not_43_out, not_44_out, not_45_out, not_46_out, not_47_out, not_48_out, not_49_out,
       not_50_out, not_51_out, not_52_out, not_53_out;

  not not_1 (not_1_out, OP5);
  not not_2 (not_2_out, OP4);
  not not_3 (not_3_out, OP2);
  not not_4 (not_4_out, OP1);
  not not_5 (not_5_out, OP0);
  not not_6 (not_6_out, OP5);
  not not_7 (not_7_out, OP4);
  not not_8 (not_8_out, OP2);
  not not_9 (not_9_out, OP1);
  not not_10 (not_10_out, OP5);
  not not_11 (not_11_out, OP4);
  not not_12 (not_12_out, OP1);
  not not_13 (not_13_out, OP0);
  not not_14 (not_14_out, OP5);
  not not_15 (not_15_out, OP4);
  not not_16 (not_16_out, OP1);
  not not_17 (not_17_out, OP4);
  not not_18 (not_18_out, OP3);
  not not_19 (not_19_out, OP2);
  not not_20 (not_20_out, OP4);
  not not_21 (not_21_out, OP2);
  not not_22 (not_22_out, OP5);
  not not_23 (not_23_out, OP4);
  not not_24 (not_24_out, OP3);
  not not_25 (not_25_out, OP1);
  not not_26 (not_26_out, OP0);
  not not_27 (not_27_out, OP5);
  not not_28 (not_28_out, OP4);
  not not_29 (not_29_out, OP3);
  not not_30 (not_30_out, OP1);
  not not_31 (not_31_out, OP5);
  not not_32 (not_32_out, OP4);
  not not_33 (not_33_out, OP2);
  not not_34 (not_34_out, OP0);
  not not_35 (not_35_out, OP5);
  not not_36 (not_36_out, OP4);
  not not_37 (not_37_out, OP3);
  not not_38 (not_38_out, OP2);
  not not_39 (not_39_out, OP0);
  not not_40 (not_40_out, OP5);
  not not_41 (not_41_out, OP4);
  not not_42 (not_42_out, OP3);
  not not_43 (not_43_out, OP2);
  not not_44 (not_44_out, OP5);
  not not_45 (not_45_out, OP4);
  not not_46 (not_46_out, OP5);
  not not_47 (not_47_out, OP4);
  not not_48 (not_48_out, OP3);
  not not_49 (not_49_out, OP0);
  not not_50 (not_50_out, OP4);
  not not_51 (not_51_out, OP3);
  not not_52 (not_52_out, OP2);
  not not_53 (not_53_out, OP1);
  and and_1 (AddI, not_1_out, not_2_out, OP3, not_3_out, not_4_out, not_5_out);
  and and_2 (AddIU, not_6_out, not_7_out, OP3, not_8_out, not_9_out, OP0);
  and and_3 (AndI, not_10_out, not_11_out, OP3, OP2, not_12_out, not_13_out);
  and and_4 (OrI, not_14_out, not_15_out, OP3, OP2, not_16_out, OP0);
  and and_5 (Lw, OP5, not_17_out, not_18_out, not_19_out, OP1, OP0);
  and and_6 (Sw, OP5, not_20_out, OP3, not_21_out, OP1, OP0);
  and and_7 (Beq, not_22_out, not_23_out, not_24_out, OP2, not_25_out, not_26_out);
  and and_8 (Bne, not_27_out, not_28_out, not_29_out, OP2, not_30_out, OP0);
  and and_9 (SltI, not_31_out, not_32_out, OP3, not_33_out, OP1, not_34_out);
  and and_10 (J, not_35_out, not_36_out, not_37_out, not_38_out, OP1, not_39_out);
  and and_11 (JAL, not_40_out, not_41_out, not_42_out, not_43_out, OP1, OP0);
  and and_12 (LUI, not_44_out, not_45_out, OP3, OP2, OP1, OP0);
  and and_13 (BLEZ, not_46_out, not_47_out, not_48_out, OP2, OP1, not_49_out);
  and and_14 (LH, OP5, not_50_out, not_51_out, not_52_out, not_53_out, OP0);
endmodule

module Instructtion_type (
  input  [5:0] OP,
  input  clk,
  output [9:0] out_3,
  output [9:0] out_4,
  output [5:0] J_type
);

  wire nor_1_out, nor_2_out, nor_3_out, not_1_out, not_2_out, not_3_out, not_4_out, not_5_out, or_1_out,
       subtractor_1_bout;
  wire [9:0] counter_1_q;

  Subtractor #(.width(6)) subtractor_1 (.a(OP), .b(6'b000011), .bout(subtractor_1_bout));  // open: out, bin
  not not_1 (not_1_out, OP[0]);
  not not_2 (not_2_out, OP[1]);
  nor nor_1 (nor_1_out, OP[0], OP[1], OP[2], OP[3], OP[4], OP[5]);
  nor nor_2 (nor_2_out, not_1_out, not_2_out, OP[2], OP[3], OP[4], OP[5]);
  nor nor_3 (nor_3_out, OP[0], not_2_out, OP[2], OP[3], OP[4], OP[5]);
  not not_3 (not_3_out, subtractor_1_bout);
  or or_1 (or_1_out, nor_2_out, nor_3_out);
  not not_4 (not_4_out, nor_1_out);
  Counter #(.width(10), .max('h3ff)) counter_1 (
    .load(not_4_out), .D(counter_1_q), .count(nor_1_out), .Q(counter_1_q), .clk(clk));  // open: carry, clr
  Counter #(.width(10), .max('h3ff)) counter_2 (
    .load(subtractor_1_bout), .D(out_4), .count(not_3_out), .Q(out_4), .clk(clk));  // open: carry, clr
  not not_5 (not_5_out, or_1_out);
  Counter #(.width(6), .max('h3f)) counter_3 (
    .load(not_5_out), .D(J_type), .count(or_1_out), .Q(J_type), .clk(clk));  // open: carry, clr
  Adder #(.width(10)) adder_1 (.a(counter_1_q), .b(10'h1), .out(out_3));  // open: cin, cout
endmodule

module Interruption (
  input  IR1,
  input  IR2,
  input  IR3,
  input  clk,
  output [1:0] out_5,
  output IR
);

  wire INM1, INM2, not_1_out, not_2_out, not_3_out, register_1_q, register_2_q, register_3_q, register_4_q,
       register_5_q, register_6_q;
  wire [1:0] multiplexer_1_out, multiplexer_2_out;

  Multiplexer #(.width(2), .enable("false")) multiplexer_1 (
    .in0(2'b00), .in1(2'b01), .out(multiplexer_1_out), .sel(IR1));
  Multiplexer #(.width(2), .enable("false")) multiplexer_2 (
    .in0(multiplexer_1_out), .in1(2'b10), .out(multiplexer_2_out), .sel(IR2));
  or or_1 (IR, IR1, IR2, IR3);
  Multiplexer #(.width(2), .enable("false")) multiplexer_3 (
    .in0(multiplexer_2_out), .in1(2'b11), .out(out_5), .sel(IR3));
  or or_2 (INM1, IR1, IR2, IR3);
  or or_3 (INM2, IR2, IR3);
  Register #(.width(1)) register_1 (.D(IR1), .en(1'b1), .Q(register_1_q), .clk(clk));  // open: clr
  Register #(.width(1)) register_2 (.D(IR2), .en(1'b1), .Q(register_2_q), .clk(clk));  // open: clr
  Register #(.width(1)) register_3 (.D(IR3), .en(1'b1), .Q(register_3_q), .clk(clk));  // open: clr
  Register #(.width(1)) register_4 (.D(INM1), .en(1'b1), .Q(register_4_q), .clk(clk));  // open: clr
  Register #(.width(1)) register_5 (.D(INM2), .en(1'b1), .Q(register_5_q), .clk(clk));  // open: clr
  Register #(.width(1)) register_6 (.D(IR3), .en(1'b1), .Q(register_6_q), .clk(clk));  // open: clr
  not not_1 (not_1_out, register_4_q);
  not not_2 (not_2_out, register_5_q);
  not not_3 (not_3_out, register_6_q);
  // AND_Gate and_1 has open pins: in0=register_1_q, in1=not_1_out, out=open
  // AND_Gate and_2 has open pins: in0=register_2_q, in1=not_2_out, out=open
  // AND_Gate and_3 has open pins: in0=register_3_q, in1=not_3_out, out=open

  // Other names for the same wires on the sheet: INM3 = IR3
endmodule

module CP0 (
  input  ExpSrc0,
  input  ExpSrc1,
  input  ExpSrc2,
  input  clk,
  input  enable,
  input  [31:0] Inst,
  input  [31:0] PCin,
  input  [31:0] Din,
  output ExRegWrite,
  output IsEret,
  output ExpBlock,
  output HasExp,
  output [31:0] PCout,
  output [31:0] Dout
);

  wire and_4_out, and_5_out, and_6_out, counter_1_q, counter_2_q, demultiplexer_1_out0, demultiplexer_1_out1,
       ExpClick, not_2_out, not_3_out, or_1_out, or_2_out;
  wire [31:0] Cause_q, controlled_buffer_1_out, multiplexer_1_out;
  wire [31:1] Status_q;

  or or_1 (or_1_out, ExpSrc0, ExpSrc1, ExpSrc2);
  and and_1 (ExpClick, or_1_out, ~ExpBlock);  // AND_Gate
  not not_1 (ExRegWrite, Inst[23]);
  and and_2 (IsEret, ~Inst[5], Inst[4], Inst[3], ~Inst[2], ~Inst[1], ~Inst[0]);  // AND_Gate
  Counter #(.width(1), .max('h1), .ongoal("stay")) counter_1 (
    .Q(counter_1_q), .clk(ExpClick), .clr(counter_2_q));  // open: load, D, count, carry
  and and_3 (HasExp, clk, counter_1_q);
  Counter #(.width(1), .max('h1), .ongoal("stay"), .trigger("falling")) counter_2 (
    .Q(counter_2_q), .clk(HasExp), .clr(not_2_out));  // open: load, D, count, carry
  not not_2 (not_2_out, counter_1_q);
  not not_3 (not_3_out, HasExp);
  Multiplexer #(.width(32), .enable("false")) multiplexer_1 (
    .in0(PCin), .in1(Din), .out(multiplexer_1_out), .sel(not_3_out));
  Demultiplexer #(.disabled(0), .enable("false")) demultiplexer_1 (
    .out0(demultiplexer_1_out0), .out1(demultiplexer_1_out1), .in(1'b1), .sel(Inst[11]));
  assign controlled_buffer_1_out = ExpSrc0 ? {32{1'b0}} : 32'bz;  // Controlled_Buffer controlled_buffer_1
  assign controlled_buffer_1_out = ExpSrc1 ? 32'h1 : 32'bz;  // Controlled_Buffer controlled_buffer_2
  assign controlled_buffer_1_out = ExpSrc2 ? 32'h2 : 32'bz;  // Controlled_Buffer controlled_buffer_3
  and and_4 (and_4_out, demultiplexer_1_out0, and_5_out);
  and and_5 (and_5_out, enable, ~ExRegWrite);  // AND_Gate
  and and_6 (and_6_out, and_5_out, demultiplexer_1_out1);
  Register #(.width(32), .trigger("high")) EPC (
    .D(multiplexer_1_out), .en(or_2_out), .Q(PCout), .clk(clk));  // open: clr
  or or_2 (or_2_out, HasExp, and_4_out);
  Register #(.width(32)) Status (.D(Din), .en(and_6_out), .Q({Status_q, ExpBlock}), .clk(clk));  // open: clr
  Register #(.width(32)) Cause (.D(controlled_buffer_1_out), .Q(Cause_q), .clk(ExpClick));  // open: en, clr
  Multiplexer #(.select(2), .width(32), .enable("false")) multiplexer_2 (
    .in0(PCout), .in1({Status_q, ExpBlock}), .in2(Cause_q), .in3({32{1'b0}}), .out(Dout), .sel(Inst[12:11]));

  // Other names for the same wires on the sheet: Sel[1:0] = Inst[12:11]
endmodule

module Priority (
  input  IR1,
  input  IR2,
  input  IR3,
  input  clk,
  input  [2:0] IM,
  output [1:0] out_6
);

  wire and_1_out, and_2_out, and_3_out, and_4_out, d_ff_1_q, d_ff_2_q, d_ff_3_q, d_ff_4_q, d_ff_5_q,
       d_ff_6_q, nand_1_out, not_1_out, not_2_out;

  D_Flip_Flop d_ff_1 (.clk(clk), .D(IR3), .Q(d_ff_1_q));  // open: Qn, preset, en, reset
  D_Flip_Flop d_ff_2 (.clk(clk), .D(IR2), .Q(d_ff_2_q));  // open: Qn, preset, en, reset
  D_Flip_Flop d_ff_3 (.clk(clk), .D(IR1), .Q(d_ff_3_q));  // open: Qn, preset, en, reset
  D_Flip_Flop d_ff_4 (.clk(clk), .D(IM[2]), .Q(d_ff_4_q));  // open: Qn, preset, en, reset
  D_Flip_Flop d_ff_5 (.clk(clk), .D(IM[1]), .Q(d_ff_5_q));  // open: Qn, preset, en, reset
  D_Flip_Flop d_ff_6 (.clk(clk), .D(IM[0]), .Q(d_ff_6_q));  // open: Qn, preset, en, reset
  and and_1 (and_1_out, d_ff_1_q, d_ff_4_q);
  and and_2 (and_2_out, d_ff_2_q, d_ff_5_q);
  and and_3 (and_3_out, d_ff_3_q, d_ff_6_q);
  not not_1 (not_1_out, and_1_out);
  nand nand_1 (nand_1_out, not_1_out, and_2_out);
  not not_2 (not_2_out, nand_1_out);
  and and_4 (and_4_out, nand_1_out, not_1_out, and_3_out);
  Priority_Encoder #(.select(2)) priority_encoder_1 (
    .in0(1'b1), .in1(and_4_out), .in2(not_2_out), .in3(and_1_out), .out(out_6));
endmodule

module Stack (
  input  in_1,
  input  in_2,
  input  [1:0] in_3,
  output [1:0] Out
);

  wire pop;
  wire [1:0] transmission_1_p4, transmission_2_p4, transmission_3_p4, transmission_4_p4, transmission_5_p4;

  // Transmission_Gate #(.width(2)) transmission_1: pin names not known; wires that end beside it: in_3, pop, in_2, transmission_1_p4
  Register #(.width(2)) register_1 (.D(transmission_1_p4), .Q(Out), .clk(in_1));  // open: en, clr
  // Transmission_Gate #(.width(2)) transmission_2: pin names not known; wires that end beside it: transmission_1_p4, in_2, pop, transmission_2_p4
  // Probe on transmission_3_p4
  // Transmission_Gate #(.width(2)) transmission_3: pin names not known; wires that end beside it: Out, pop, in_2, transmission_3_p4
  Register #(.width(2)) register_2 (.D(transmission_3_p4), .Q(transmission_2_p4), .clk(in_1));  // open: en, clr
  not not_1 (pop, in_2);
  // Transmission_Gate #(.width(2)) transmission_4: pin names not known; wires that end beside it: transmission_2_p4, pop, in_2, transmission_4_p4
  // Transmission_Gate #(.width(2)) transmission_5: pin names not known; wires that end beside it: transmission_3_p4, in_2, pop, transmission_5_p4
  // Transmission_Gate #(.width(2)) transmission_6: pin names not known; wires that end beside it: transmission_4_p4, in_2, pop, 2'b00
  Register #(.width(2)) register_3 (.D(transmission_4_p4), .Q(transmission_5_p4), .clk(in_1));  // open: en, clr

  // Other names for the same wires on the sheet: clk = in_1; push = in_2
endmodule

module ExpPri (
  input  IR1,
  input  IR2,
  input  IR3,
  input  clk
);
endmodule
