// Logisim project CS1410_U201414830_方成_regfile.circ as structural Verilog: 2 circuits, main circuit main
module main (
  input  [4:0] Reg1_num,
  input  [4:0] Reg2,
  input  [4:0] Write_Reg_num,
  input  [31:0] Din,
  input  Write_Enable,
  input  Clock,
  output [31:0] Reg1,
  output [31:0] s0_Value,
  output [31:0] s1_Value,
  output [31:0] s2_Value,
  output [31:0] ra_Value,
  output [31:0] ra_Value_2,
  output [31:0] Reg2_2
);

  wire and_1_out, and_2_out, and_3_out, and_4_out, and_5_out, and_6_out, and_7_out, and_8_out, and_9_out,
       and_10_out, and_11_out, and_12_out, and_13_out, and_14_out, and_15_out, and_16_out, and_17_out,
       and_18_out, and_19_out, and_20_out, and_21_out, and_22_out, and_23_out, and_24_out, and_25_out,
       and_26_out, and_27_out, and_28_out, and_29_out, and_30_out, and_31_out, and_32_out, decoder_1_out0,
       decoder_1_out1, decoder_1_out2, decoder_1_out3, decoder_1_out4, decoder_1_out5, decoder_1_out6,
       decoder_1_out7, decoder_1_out8, decoder_1_out9, decoder_1_out10, decoder_1_out11, decoder_1_out12,
       decoder_1_out13, decoder_1_out14, decoder_1_out15, decoder_1_out16, decoder_1_out17, decoder_1_out18,
       decoder_1_out19, decoder_1_out20, decoder_1_out21, decoder_1_out22, decoder_1_out23, decoder_1_out24,
       decoder_1_out25, decoder_1_out26, decoder_1_out27, decoder_1_out28, decoder_1_out29, decoder_1_out30,
       decoder_1_out31;
  wire [31:0] _0_q, _1_q, _2_q, _3_q, _5_q, _6_q, _7_q, _8_q, _9_q, _10_q, _11_q, _12_q, _13_q, _14_q, _15_q,
       _16_q, _19_q, _20_q, _21_q, _22_q, _23_q, _24_q, _25_q, _26_q, _27_q, _28_q, _30_q;

  Decoder #(.select(5), .enable("false")) decoder_1 (
    .out0(decoder_1_out0), .out1(decoder_1_out1), .out2(decoder_1_out2), .out3(decoder_1_out3),
    .out4(decoder_1_out4), .out5(decoder_1_out5), .out6(decoder_1_out6), .out7(decoder_1_out7),
    .out8(decoder_1_out8), .out9(decoder_1_out9), .out10(decoder_1_out10), .out11(decoder_1_out11),
    .out12(decoder_1_out12), .out13(decoder_1_out13), .out14(decoder_1_out14), .out15(decoder_1_out15),
    .out16(decoder_1_out16), .out17(decoder_1_out17), .out18(decoder_1_out18), .out19(decoder_1_out19),
    .out20(decoder_1_out20), .out21(decoder_1_out21), .out22(decoder_1_out22), .out23(decoder_1_out23),
    .out24(decoder_1_out24), .out25(decoder_1_out25), .out26(decoder_1_out26), .out27(decoder_1_out27),
    .out28(decoder_1_out28), .out29(decoder_1_out29), .out30(decoder_1_out30), .out31(decoder_1_out31),
    .sel(Write_Reg_num));
  and and_1 (and_1_out, decoder_1_out0, Write_Enable);
  and and_2 (and_2_out, decoder_1_out1, Write_Enable);
  and and_3 (and_3_out, decoder_1_out2, Write_Enable);
  and and_4 (and_4_out, decoder_1_out3, Write_Enable);
  and and_5 (and_5_out, decoder_1_out4, Write_Enable);
  and and_6 (and_6_out, decoder_1_out5, Write_Enable);
  and and_7 (and_7_out, decoder_1_out6, Write_Enable);
  and and_8 (and_8_out, decoder_1_out7, Write_Enable);
  and and_9 (and_9_out, decoder_1_out8, Write_Enable);
  and and_10 (and_10_out, decoder_1_out9, Write_Enable);
  and and_11 (and_11_out, decoder_1_out10, Write_Enable);
  and and_12 (and_12_out, decoder_1_out11, Write_Enable);
  and and_13 (and_13_out, decoder_1_out12, Write_Enable);
  and and_14 (and_14_out, decoder_1_out13, Write_Enable);
  and and_15 (and_15_out, decoder_1_out14, Write_Enable);
  and and_16 (and_16_out, decoder_1_out15, Write_Enable);
  and and_17 (and_17_out, decoder_1_out16, Write_Enable);
  and and_18 (and_18_out, decoder_1_out17, Write_Enable);
  and and_19 (and_19_out, decoder_1_out18, Write_Enable);
  and and_20 (and_20_out, decoder_1_out19, Write_Enable);
  and and_21 (and_21_out, decoder_1_out20, Write_Enable);
  and and_22 (and_22_out, decoder_1_out21, Write_Enable);
  and and_23 (and_23_out, decoder_1_out22, Write_Enable);
  and and_24 (and_24_out, decoder_1_out23, Write_Enable);
  and and_25 (and_25_out, decoder_1_out24, Write_Enable);
  and and_26 (and_26_out, decoder_1_out25, Write_Enable);
  and and_27 (and_27_out, decoder_1_out26, Write_Enable);
  and and_28 (and_28_out, decoder_1_out27, Write_Enable);
  and and_29 (and_29_out, decoder_1_out28, Write_Enable);
  and and_30 (and_30_out, decoder_1_out29, Write_Enable);
  and and_31 (and_31_out, decoder_1_out30, Write_Enable);
  and and_32 (and_32_out, decoder_1_out31, Write_Enable);
  Register #(.width(32)) _0 (.D({32{1'b0}}), .en(and_1_out), .Q(_0_q), .clk(Clock));  // open: clr
  Register #(.width(32)) _1 (.D(Din), .en(and_2_out), .Q(_1_q), .clk(Clock));  // open: clr
  Register #(.width(32)) _2 (.D(Din), .en(and_3_out), .Q(_2_q), .clk(Clock));  // open: clr
  Register #(.width(32)) _3 (.D(Din), .en(and_4_out), .Q(_3_q), .clk(Clock));  // open: clr
  Register #(.width(32)) _4 (.D(Din), .en(and_5_out), .Q(s0_Value), .clk(Clock));  // open: clr
  Register #(.width(32)) _5 (.D(Din), .en(and_6_out), .Q(_5_q), .clk(Clock));  // open: clr
  Register #(.width(32)) _6 (.D(Din), .en(and_7_out), .Q(_6_q), .clk(Clock));  // open: clr
  Register #(.width(32)) _7 (.D(Din), .en(and_8_out), .Q(_7_q), .clk(Clock));  // open: clr
  Register #(.width(32)) _8 (.D(Din), .en(and_9_out), .Q(_8_q), .clk(Clock));  // open: clr
  Register #(.width(32)) _9 (.D(Din), .en(and_10_out), .Q(_9_q), .clk(Clock));  // open: clr
  Register #(.width(32)) _10 (.D(Din), .en(and_11_out), .Q(_10_q), .clk(Clock));  // open: clr
  Register #(.width(32)) _11 (.D(Din), .en(and_12_out), .Q(_11_q), .clk(Clock));  // open: clr
  Register #(.width(32)) _12 (.D(Din), .en(and_13_out), .Q(_12_q), .clk(Clock));  // open: clr
  Register #(.width(32)) _13 (.D(Din), .en(and_14_out), .Q(_13_q), .clk(Clock));  // open: clr
  Register #(.width(32)) _14 (.D(Din), .en(and_15_out), .Q(_14_q), .clk(Clock));  // open: clr
  Register #(.width(32)) _15 (.D(Din), .en(and_16_out), .Q(_15_q), .clk(Clock));  // open: clr
  Register #(.width(32)) _16 (.D(Din), .en(and_17_out), .Q(_16_q), .clk(Clock));  // open: clr
  Register #(.width(32)) _17 (.D(Din), .en(and_18_out), .Q(s1_Value), .clk(Clock));  // open: clr
  Register #(.width(32)) _18 (.D(Din), .en(and_19_out), .Q(s2_Value), .clk(Clock));  // open: clr
  Register #(.width(32)) _19 (.D(Din), .en(and_20_out), .Q(_19_q), .clk(Clock));  // open: clr
  Register #(.width(32)) _20 (.D(Din), .en(and_21_out), .Q(_20_q), .clk(Clock));  // open: clr
  Register #(.width(32)) _21 (.D(Din), .en(and_22_out), .Q(_21_q), .clk(Clock));  // open: clr
  Register #(.width(32)) _22 (.D(Din), .en(and_23_out), .Q(_22_q), .clk(Clock));  // open: clr
  Register #(.width(32)) _23 (.D(Din), .en(and_24_out), .Q(_23_q), .clk(Clock));  // open: clr
  Register #(.width(32)) _24 (.D(Din), .en(and_25_out), .Q(_24_q), .clk(Clock));  // open: clr
  Register #(.width(32)) _25 (.D(Din), .en(and_26_out), .Q(_25_q), .clk(Clock));  // open: clr
  Register #(.width(32)) _26 (.D(Din), .en(and_27_out), .Q(_26_q), .clk(Clock));  // open: clr
  Register #(.width(32)) _27 (.D(Din), .en(and_28_out), .Q(_27_q), .clk(Clock));  // open: clr
  Register #(.width(32)) _28 (.D(Din), .en(and_29_out), .Q(_28_q), .clk(Clock));  // open: clr
  Register #(.width(32)) _29 (.D(Din), .en(and_30_out), .Q(ra_Value_2), .clk(Clock));  // open: clr
  Register #(.width(32)) _30 (.D(Din), .en(and_31_out), .Q(_30_q), .clk(Clock));  // open: clr
  Register #(.width(32)) _31 (.D(Din), .en(and_32_out), .Q(ra_Value), .clk(Clock));  // open: clr
  Multiplexer #(.select(5), .width(32), .enable("false")) multiplexer_1 (
    .in0(_0_q), .in1(_1_q), .in2(_2_q), .in3(_3_q), .in4(s0_Value), .in5(_5_q), .in6(_6_q), .in7(_7_q),
    .in8(_8_q), .in9(_9_q), .in10(_10_q), .in11(_11_q), .in12(_12_q), .in13(_13_q), .in14(_14_q),
    .in15(_15_q), .in16(_16_q), .in17(s1_Value), .in18(s2_Value), .in19(_19_q), .in20(_20_q), .in21(_21_q),
    .in22(_22_q), .in23(_23_q), .in24(_24_q), .in25(_25_q), .in26(_26_q), .in27(_27_q), .in28(_28_q),
    .in29(ra_Value_2), .in30(_30_q), .in31(ra_Value), .out(Reg1), .sel(Reg1_num));
  Multiplexer #(.select(5), .width(32), .enable("false")) multiplexer_2 (
    .in0(_0_q), .in1(_1_q), .in2(_2_q), .in3(_3_q), .in4(s0_Value), .in5(_5_q), .in6(_6_q), .in7(_7_q),
    .in8(_8_q), .in9(_9_q), .in10(_10_q), .in11(_11_q), .in12(_12_q), .in13(_13_q), .in14(_14_q),
    .in15(_15_q), .in16(_16_q), .in17(s1_Value), .in18(s2_Value), .in19(_19_q), .in20(_20_q), .in21(_21_q),
    .in22(_22_q), .in23(_23_q), .in24(_24_q), .in25(_25_q), .in26(_26_q), .in27(_27_q), .in28(_28_q),
    .in29(ra_Value_2), .in30(_30_q), .in31(ra_Value), .out(Reg2_2), .sel(Reg2));

  // Other names for the same wires on the sheet: clk = Clock; ra[31:0] = ra_Value; reg2_num[4:0] = Reg2;
  //   reg2_t[31:0] = Reg2_2; s0[31:0] = s0_Value; s1[31:0] = s1_Value; s2[31:0] = s2_Value; sp[31:0] = ra_Value_2;
  //   WE = Write_Enable; write_data[31:0] = Din

  // Notes on the sheet:
  //   输入引脚
  //   输出引脚
  //   Debug引脚，便于观测寄存器值
  //   请勿修改引脚以及封装，直接使用隧道连接电路
endmodule

module test (
);

  wire and_1_out, clock_1_out, counter_1_carry, not_1_out, not_2_out, not_3_out, not_4_out, not_5_out;
  wire [3:0] main_1_reg1_2;
  wire [5:0] adder_1_out, counter_1_q, multiplexer_1_out;
  wire [31:0] alu_1_result, main_1_reg1, multiplexer_2_out, ram_1_data;

  not not_1 (not_1_out, and_1_out);
  and and_1 (and_1_out, not_2_out, clock_1_out);
  Counter #(.width(6), .max('h20)) counter_1 (
    .load(1'b0), .D({6{1'b0}}), .count(1'b1), .Q(counter_1_q), .carry(counter_1_carry), .clk(not_1_out),
    .clr(1'b0));
  not not_2 (not_2_out, counter_1_carry);
  Clock clock_1 (.out(clock_1_out));
  Adder #(.width(6)) adder_1 (.a(6'b100000), .b(counter_1_q), .out(adder_1_out), .cin(1'b0));  // open: cout
  // Probe on counter_1_q
  Multiplexer #(.width(6)) multiplexer_1 (
    .in0(counter_1_q), .in1(adder_1_out), .out(multiplexer_1_out), .sel(not_3_out), .en(1'b1));
  not not_3 (not_3_out, not_1_out);
  // Probe on multiplexer_1_out
  not not_4 (not_4_out, not_1_out);
  RAM #(.addrWidth(6), .dataWidth(32), .bus("separate")) ram_1 (
    .addr(multiplexer_1_out), .din({main_1_reg1[31:8], main_1_reg1_2, main_1_reg1[3:0]}), .data(ram_1_data),
    .str(not_4_out), .clk(not_1_out), .ld(not_1_out), .clr(1'b0));  // open: sel
  // Probe on ram_1_data
  Hex_Digit_Display hex_digit_display_1 (.value(main_1_reg1[27:24]), .dp(1'b0));
  Hex_Digit_Display hex_digit_display_2 (.value(main_1_reg1[31:28]), .dp(1'b0));
  Multiplexer #(.width(32)) multiplexer_2 (
    .in0({32{1'b0}}), .in1(ram_1_data), .out(multiplexer_2_out), .sel(not_1_out), .en(1'b1));
  // Probe on multiplexer_2_out
  Hex_Digit_Display hex_digit_display_3 (.value(main_1_reg1[23:20]), .dp(1'b0));
  ALU alu_1 (
    .AluOP(4'b0101), .X({main_1_reg1[31:8], main_1_reg1_2, main_1_reg1[3:0]}), .Result(alu_1_result),
    .Y(multiplexer_2_out));  // open: Equal, Signed_Overflow, Result_2, UnSigned_Overflow
  Hex_Digit_Display hex_digit_display_4 (.value(main_1_reg1[15:12]), .dp(1'b0));
  Hex_Digit_Display hex_digit_display_5 (.value(main_1_reg1[19:16]), .dp(1'b0));
  // Probe on alu_1_result
  Hex_Digit_Display hex_digit_display_6 (.value(main_1_reg1[11:8]), .dp(1'b0));
  Hex_Digit_Display hex_digit_display_7 (.value(main_1_reg1_2), .dp(1'b0));
  main main_1 (
    .Reg1_num(5'b00001), .Write_Reg_num(5'b00001), .Din(alu_1_result), .Write_Enable(1'b1),
    .Clock(not_5_out), .Reg1({main_1_reg1[31:8], main_1_reg1_2, main_1_reg1[3:0]}));  // open: Reg2, Reg2_2, s0_Value, s1_Value, s2_Value, ra_Value, ra_Value_2
  not not_5 (not_5_out, not_1_out);
  Hex_Digit_Display hex_digit_display_8 (.value(main_1_reg1[3:0]), .dp(1'b0));
  // Probe on {main_1_reg1[31:8], main_1_reg1_2, main_1_reg1[3:0]}
endmodule
